# Fritzing sketch esp32_infrared_sensor (saved by Fritzing 0.9.6b)

parts:
  M1 = DOIT Esp32 DevKit v1 (30 pins long, 11 pins width) [part_number=ESP32S-PIN30]
  J1 = Infrared Proximity Sensor

nets:
  3V3: M1.3V3, J1.Vcc
  GND: M1.GND, J1.GND
  N1: M1.D34, J1.Vout

notes:
  ADC1_6

custom parts:
  DOIT Esp32 DevKit v1 (30 pins long, 11 pins width): The DOIT Esp32 DevKit v1 is one of the development board created by DOIT to evaluate the ESP-WROOM-32 module. It is based on the ESP32 microcontroller that boasts Wifi, Bluetooth, Ethernet and Low Power support all in a single chip. (vanepp) made breadboard work, adjusted pin numbering and labels and reduced size of schematic and cleaned up pcb. This chip is 30pins long (2 x15) and 11 pins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
